# Fritzing sketch finalFritzingCeng317 (saved by Fritzing 0.9.3b)
circuit board: 15.1063cm x 9.52737cm
breadboards: 1

parts:
  Raspberry_Pi_2 = Raspberry Pi 3 [part_number=RPI-3-V1.2]
  Driver = DRV 8825 Stepper Motor Carrier, High Current [part_number="DRV 8825"]
  Motor = Stepper Motor - Bipolar
  part = Electrolytic Capacitor [capacitance=100µF package="200 mil [THT, electrolytic]"]

nets:
  3V3: Raspberry_Pi_2.3v3, Raspberry_Pi_2.3V3, Driver.RESET, Driver.SLEEP
  N1: Raspberry_Pi_2.GPIO21, Driver.STEP
  N2: Raspberry_Pi_2.GPIO20, Driver.DIRECTION
  N3: Raspberry_Pi_2.GND, Driver.GROUND_LOG
  N4: Raspberry_Pi_2.GPIO18, Driver.MS3
  N5: Raspberry_Pi_2.GPIO15, Driver.MS2
  N6: Raspberry_Pi_2.GPIO14, Driver.MS1
  N7: Driver.VOLTAGE_ST/_MT, part.+
  N8: Driver.GROUND_ST/_MT, part.-
  N9: Driver.OUT_2B, Motor.D
  N10: Driver.OUT_2A, Motor.C
  N11: Driver.OUT_1A, Motor.A
  N12: Driver.OUT_1B, Motor.B

notes:
  Navkiran Kaur
  capacitor
  A
  C
  B
  D
  2B
  2A
  1A
  1B
  MS1
  MS2
  MS3
  RST
  SLP
  STEP
  DIR
  GIPO14
  GIPO15
  GIPO18
  GIPO20
  GIPO21
  GND
  V
  3.3 V
  Raspberry pie
  Bipolar stepper motor
  Motor
  Rpi3
