# Fritzing sketch final_fritzingCeng317 (saved by Fritzing 0.9.3b)
circuit board: 9.3785cm x 6.1915cm
breadboards: 1

parts:
  Raspberry_Pi_2 = Raspberry Pi 3 [part_number=RPI-3-V1.2]
  Driver = DRV 8825 Stepper Motor Carrier, High Current [part_number="DRV 8825"]
  C1 = Electrolytic Capacitor [capacitance=100µF package="200 mil [THT, electrolytic]"]
  Motor = Stepper Motor - Bipolar
  Power_plug1 = Power plug

nets:
  3V3: Raspberry_Pi_2.3v3, Raspberry_Pi_2.3V3, Driver.RESET, Driver.SLEEP
  N1: Raspberry_Pi_2.GPIO21, Driver.STEP
  N2: Raspberry_Pi_2.GPIO20, Driver.DIRECTION
  GND: Raspberry_Pi_2.GND, Driver.GROUND_ST/_MT, Driver.GROUND_LOG, C1.-, Power_plug1.GND
  N3: Raspberry_Pi_2.GPIO18, Driver.MS3
  N4: Raspberry_Pi_2.GPIO15, Driver.MS2
  N5: Raspberry_Pi_2.GPIO14, Driver.MS1
  N6: Driver.VOLTAGE_ST/_MT, C1.+, Power_plug1.VCC
  N7: Driver.OUT_2B, Motor.A
  N8: Driver.OUT_2A, Motor.C
  N9: Driver.OUT_1A, Motor.B
  N10: Driver.OUT_1B, Motor.D

notes:
  Navkiran Kaur
  capacitor
  2B
  2A
  1A
  1B
  MS1
  MS2
  MS3
  RST
  SLP
  STEP
  DIR
  GIPO14
  GIPO15
  GIPO18
  GIPO20
  GIPO21
  GND
  V
  Raspberry pie
  Bipolar stepper motor
  Motor
  Rpi3
  12 v power supply
